# Fritzing sketch Schematic-180826 (saved by Fritzing 0.9.3b)

parts:
  U1 = NodeMCU V1.0
  U4 = MAX485 [package=dil08]
  J1 = Screw terminal - 2 pins [package=THT]  # not connected
  J2 = Screw terminal - 2 pins [package=THT]

nets:
  N1: U1.RX, U4.RO
  N2: U1.GND, U4.RE
  N3: U1.3V3, U4.A
  N4: U4.B, J2.pin2
  N5: U4.VCC, J2.pin1

notes:
  Eltako
  Multisensor MS
  1
  2
  A
  B
  RO
  RE
  DE
  MAX485
  DI
  VCC
  GND

custom parts:
  NodeMCU V1.0: ESP8266 based NodeMCU
